// Logisim project nand2tetris.circ as structural Verilog: 3 circuits, main circuit main
module main (
  input  in_1,
  output out_2
);

  AndGate andgate_1 ();  // open: a, b, outp
  NotGate notgate_1 (.inp(in_1), .outp(out_2));
endmodule

module NotGate (
  input  inp,
  output outp
);

  nand nand_1 (outp, inp, inp);
endmodule

module AndGate (
  input  a,
  input  b,
  output outp
);

  wire nand_1_out;

  nand nand_1 (nand_1_out, a, b);
  NotGate notgate_1 (.inp(nand_1_out), .outp(outp));
endmodule
